// Logisim project half_and_full_adder.circ as structural Verilog: 1 circuit, main circuit main
module main (
  input  A,
  input  B,
  input  A_2,
  input  B_2,
  input  C,
  output out_6,
  output out_7,
  output out_8,
  output AB___BC___AC
);

  wire and_2_out, and_3_out, xor_2_out;

  xor xor_1 (out_6, A, B);
  and and_1 (out_7, A, B);
  xor xor_2 (xor_2_out, A_2, B_2);
  and and_2 (and_2_out, A_2, B_2);
  xor xor_3 (out_8, xor_2_out, C);
  and and_3 (and_3_out, xor_2_out, C);
  or or_1 (AB___BC___AC, and_3_out, and_2_out);

  // Notes on the sheet:
  //   HALF ADDER
  //   FULL ADDER
  //   A'B + AB'
  //   SUM
  //   AB
  //   CARRY
  //   A + B + C
  //   SUM
  //   CARRY
endmodule
