// Logisim project half_and_full_subtractor.circ as structural Verilog: 1 circuit, main circuit main
module main (
  input  A,
  input  B,
  input  A_2,
  input  B_2,
  input  C,
  output Difference,
  output Borrow,
  output Difference_2,
  output Borrow_2
);

  wire and_1_out, and_3_out, not_1_out, not_2_out, not_3_out, xor_1_out;

  not not_1 (not_1_out, A_2);
  not not_2 (not_2_out, A);
  xor xor_1 (xor_1_out, A_2, B_2);
  and and_1 (and_1_out, not_1_out, B_2);
  xor xor_2 (Difference, A, B);
  and and_2 (Borrow, B, not_2_out);
  not not_3 (not_3_out, xor_1_out);
  xor xor_3 (Difference_2, xor_1_out, C);
  and and_3 (and_3_out, not_3_out, C);
  or or_1 (Borrow_2, and_3_out, and_1_out);

  // Notes on the sheet:
  //   Half Subtracter
  //   Full Subtractor
  //   HRIGVED
  //   09511515625
endmodule
