// Logisim project logic_gates.circ as structural Verilog: 1 circuit, main circuit main
module main (
  input  in_1,
  input  in_2,
  input  in_3,
  input  in_4,
  input  in_5,
  input  in_6,
  input  in_7,
  input  in_8,
  input  in_9,
  input  in_10,
  input  in_11,
  output out_12,
  output out_13,
  output out_14,
  output out_15,
  output out_16,
  output out_17
);

  not not_1 (out_12, in_1);
  and and_1 (out_13, in_2, in_3);
  or or_1 (out_14, in_4, in_5);
  nand nand_1 (out_15, in_6, in_7);
  nor nor_1 (out_16, in_8, in_9);
  xor xor_1 (out_17, in_10, in_11);

  // Notes on the sheet:
  //   NOT GATE
  //   AND GATE
  //   OR GATE
  //   NAND GATE
  //   NOR GATE
  //   XOR GATE
endmodule
